# Fritzing sketch lesson5-diagram (saved by Fritzing 0.9.3b)
breadboards: 1

parts:
  Part1 = Photon
  DS1 = DS18B20 1-Wire Temperature Sensor [part_number=DS18B20]
  R1 = PHOTOCELL [package=photocell]

nets:
  GND: Part1.A1, Part1.GND, DS1.GND, R1.P$1
  N1: Part1.A5, R1.P$2
  N2: Part1.D3, DS1.DQ
  3V3: Part1.3V3, DS1.VDD
